# Fritzing sketch schema electrica (saved by Fritzing 0.9.3b)
breadboards: 1

parts:
  Driver_1_L298N = L298N DC motor driver
  Driver_2_L298N = L298N DC motor driver
  MOTOR_DC_2 = DC Motor
  MOTOR_DC_1 = DC Motor
  MOTOR_DC_3 = DC Motor
  Buton_ON-OFF = Toggle Switch spst [package=THT]
  Parte1 = Arduino Mega 2560 (Rev3)
  Modul_HC-12 = HC-12 Module
  Antenna1 = HC-12 Antenna
  Modul_HC-12_2 = HC-12 Module
  Antenna2 = HC-12 Antenna
  Arduino_NANO = Arduino Nano (Rev3.0)
  Modul_Joystick = Black Joystick KY-023
  Baterie_LiPo_4S = LIPO-2000mAh [package=lipo-2000]
  Modul_Mini360_1 = Mini-360 DC-DC Buck converter [package=THT]
  Modul_Mini360_2 = Mini-360 DC-DC Buck converter [package=THT]
  Sursa_de_lumina = 16 NeoPixel Ring [part_number=1463]
  Regulator_L7805 = Voltage Regulator [package=to-92]
  C1_220_uF/35V = Ceramic Capacitor [capacitance=100nF package="100 mil [THT, multilayer]"]
  C2 = Ceramic Capacitor [capacitance=100nF package="100 mil [THT, multilayer]"]

nets:
  N1: Driver_1_L298N.OUT1, MOTOR_DC_1.pin_2
  N2: Driver_1_L298N.OUT2, MOTOR_DC_1.pin_1
  N3: Driver_1_L298N.OUT3, MOTOR_DC_2.pin_2
  N4: Driver_1_L298N.OUT4, MOTOR_DC_2.pin_1
  N5: Driver_1_L298N.12V, Modul_Mini360_1.OUT+
  N6: Driver_1_L298N.GND, Modul_Mini360_1.OUT-
  N7: Driver_1_L298N.ENA, Parte1.D11_PWM
  N8: Driver_1_L298N.ENB, Parte1.D6_PWM
  N9: Driver_1_L298N.IN1, Parte1.D10_PWM
  N10: Driver_1_L298N.IN2, Parte1.D9_PWM
  N11: Driver_1_L298N.IN3, Parte1.D8_PWM
  N12: Driver_1_L298N.IN4, Parte1.D7_PWM
  N13: Driver_2_L298N.OUT1, MOTOR_DC_3.pin_2
  N14: Driver_2_L298N.OUT2, MOTOR_DC_3.pin_1
  12V: Driver_2_L298N.12V, Parte1.VIN, Modul_Mini360_2.OUT+, Regulator_L7805.IN, C1_220_uF/35V.1
  GND: Driver_2_L298N.GND, Modul_Mini360_2.OUT-, Regulator_L7805.GND, C1_220_uF/35V.0, C2.0
  N15: Driver_2_L298N.ENA, Parte1.D31
  N16: Driver_2_L298N.IN1, Parte1.D33
  N17: Driver_2_L298N.IN2, Parte1.D35
  N18: Buton_ON-OFF.L1, Baterie_LiPo_4S.+
  N19: Buton_ON-OFF.COM, Modul_Mini360_1.IN+, Modul_Mini360_2.IN+
  GND_2: Parte1.GND, Modul_HC-12.GND, Baterie_LiPo_4S.-, Modul_Mini360_1.IN-, Modul_Mini360_2.IN-, Sursa_de_lumina.GND
  N20: Parte1.D13_PWM, Sursa_de_lumina.IN
  5V: Parte1.5V, Modul_HC-12.VCC
  N21: Parte1.D51, Modul_HC-12.TXD
  N22: Parte1.D53, Modul_HC-12.RXD
  N23: Modul_HC-12.ANT, Antenna1.ANT
  N24: Modul_HC-12_2.TXD, Arduino_NANO.D1/TX
  N25: Modul_HC-12_2.RXD, Arduino_NANO.D0/RX
  GND_3: Modul_HC-12_2.GND, Arduino_NANO.GND, Modul_Joystick.GND
  VCC: Modul_HC-12_2.VCC, Arduino_NANO.5V, Modul_Joystick.+5V
  N26: Modul_HC-12_2.ANT, Antenna2.ANT
  N27: Arduino_NANO.A3, Modul_Joystick.VRy
  N28: Sursa_de_lumina.VDD, Regulator_L7805.OUT, C2.1

custom parts:
  L298N DC motor driver: 2x DC motor driver with 78M05 positive voltage regulator (7..35 V) L298N: max 46 V, 2 A Set 5 V Enable jumper to enable 5 V regultor (needed for the L298N) and +5 V output at screw terminal or supply external +5 V at screw terminal Set ENA and/or ENB to +5 V to enable motor permanently or supply ENA and/or ENB with PWM signal IN1 and IN2 set rotation directory for motor A (OUT1/OUT2) IN2 and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
  Toggle Switch spst: Toggle Switch single pole single throw
  HC-12 Module: HC-12 433Mhz Module
  HC-12 Antenna: Antenna for HC-12 433Mhz Module
  Black Joystick KY-023: Description: The joystick is a combination of 2 analoog potentiometer and a digital switch. Arduino GND --> Module pin - Arduino +5V --> Module pin +5V Arduino Analoog 0 --> Module VRx Arduino Analoog 1 --> Module VRy Arduino Digital --> Module SW Dimensions: 1" x 1.25"
  Mini-360 DC-DC Buck converter: Mini-360 DC-DC Buck converter. Tiny buck step down voltage converter, input voltage 4.75 to 23V output 1 to 17V adjustable. Available from ebay and the like.
  16 NeoPixel Ring: 16 ultra bright smart LED NeoPixels are arranged in a circle with 1.75" (44.5mm) outer diameter. The rings are 'chainable' - connect the output pin of one to the input pin of another. Use only one microcontroller pin to control as many as you can chain together! Each LED is addressable as the driver chip is inside the LED. Each one has ~18mA constant current drive so the color will be very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
  Voltage Regulator: TO92 78xx voltage regulator. IGO (Input Ground Output).
